// Digital circuit Processor.dig as structural Verilog
// Simple processor based on the MIPS architecture. 
// It is a Harvard single-cycle CPU.
// {{de Einfacher Prozessor, der an die MIPS-Architektur 
// angelehnt ist. Es handelt sich um eine Harvard 
// Single-Cycle CPU.}}
module Processor (
  input  Clock,
  output [15:0] A,
  output [15:0] D,
  output ioW,
  output ioR
);

  wire abs, alu2D, alu_1_p6, alu_1_p7, alu_1_p8, aluOp, br, branch_1_p1, branch_1_p4, branch_1_p5,
       branch_1_p6, iem, imm, ld, muxA, pc_1_p4, RetI, sf, src2D, st, stPC, WE;
  wire [2:0] muxB;
  wire [15:0] imreg_1_p5, multiplexer_1_out, pc_1_p5, pc_1_p6, register_1_p6, register_1_p7, rom_1_d,
       signext_1_p2, signext_1_p3, signext_1_p4;

  // PC pc_1: pin names not known; wires that end beside it: A, Clock, abs, pc_1_p4, pc_1_p5, pc_1_p6
  ROM #(.AddrBits(16), .isProgramMemory("true"), .Bits(16)) rom_1 (.A(pc_1_p6), .sel(1'b1), .D(rom_1_d));
  assign D = stPC ? pc_1_p5 : 16'bz;  // Driver driver_1
  // Control control_1: pin names not known; wires that end beside it: RetI, ioR, ioW, ld, st, br, sf, aluOp, alu2D, muxA, src2D, muxB, abs, iem, imm, WE, rom_1_d[15:8], stPC
  // Register register_1: pin names not known; wires that end beside it: D, Clock, rom_1_d[3:0], rom_1_d[7:4], WE, register_1_p6, register_1_p7
  // ImReg imreg_1: pin names not known; wires that end beside it: imm, iem, Clock, rom_1_d, imreg_1_p5, register_1_p7
  // SignExt signext_1: pin names not known; wires that end beside it: rom_1_d, signext_1_p2, signext_1_p3, signext_1_p4, muxB
  assign D = src2D ? register_1_p7 : 16'bz;  // Driver driver_2
  Multiplexer #(.Bits(16)) multiplexer_1 (
    .sel(muxA), .in_0(register_1_p6), .in_1(register_1_p7), .out(multiplexer_1_out));
  Multiplexer #(.Selector_Bits(3), .Bits(16)) multiplexer_2 (
    .sel(muxB), .in_0({16{1'b0}}), .in_1(imreg_1_p5), .in_2({16{1'b0}}), .in_3({16{1'b0}}),
    .in_4(signext_1_p2), .in_5(signext_1_p3), .in_6(signext_1_p4));  // open: in_7, out
  // Branch branch_1: pin names not known; wires that end beside it: branch_1_p1, pc_1_p4, br, branch_1_p4, branch_1_p5, branch_1_p6
  // ALU alu_1: pin names not known; wires that end beside it: multiplexer_1_out, aluOp, branch_1_p1, branch_1_p4, A, alu_1_p6, alu_1_p7, alu_1_p8
  assign D = alu2D ? A : 16'bz;  // Driver driver_3
  // Flags flags_1: pin names not known; wires that end beside it: branch_1_p4, branch_1_p5, branch_1_p6, sf, Clock, alu_1_p8, alu_1_p7, alu_1_p6
  RAMSinglePort #(.AddrBits(16), .Bits(16), .Addr_Bits(16)) mem (.A(A), .str(st), .C(Clock), .ld(ld), .D(D));
  // Graphics graphics_1: pin names not known; wires that end beside it: A, ioR, Clock, ioW, D

  // Other names for the same wires on the sheet: C = Clock

  // Notes on the sheet:
  //   Clock: Hz: 2147483647
  //   A: Address bus
  //   {{de Adressbus}}
  //   D: Data Bus
  //   {{de Datenbus}}
  //   ioW: io write enable
  //   {{de IO Schreibfreigabe}}
  //   ioR: io read enable
  //   {{de IO Lesefreigabe}}
  //   contents of rom_1 (hex, n*v repeats v):
  //   8000,961,8190,951,a90,a83,a25,a3a,10e1,afc,2bef,3d5f,c21,212f
  //   ,38f9,3d20,105,116,a30,a20,aa0,8035,3ac0,4380,2180,3505,2172,3505
  //   ,2173,3503,3d03,2173,3801,aa3,401a,c01,c11,c21,8014,2020,38eb
  //   ,c31,8014,2030,38e6,1991,ffff,3e09,146,165,154,4400,3ddb,a70,1031
  //   ,8014,f00,8060,3ab0,c21,c01,8060,3ab0,c31,8014,b00,8060,3ab0,c31
  //   ,8014,b00,8060,3ab0,1021,1001,8060,3ab0,1021,1001,8060,3ab0,1031
  //   ,8014,f00,8060,3ab0,1031,8014,f00,8060,3ab0,c21,c31,8015,b00,3b0c
  //   ,8014,2020,3707,8014,2030,3704,4380,2180,3501,c71,3b0b,143,8014
  //   ,1c40,242,246,4048,2cfe,ce1,3b0f
endmodule
